# Fritzing sketch teclado_3x4 (saved by Fritzing 0.9.3b)

parts:
  kEYPAD_MATRICIAL_1 = KEYPAD 4x3
  Part1 = Arduino Nano (Rev3.0)

nets:
  N1: kEYPAD_MATRICIAL_1.col1, Part1.D8
  N2: kEYPAD_MATRICIAL_1.arrow1, Part1.D7
  N3: kEYPAD_MATRICIAL_1.col2, Part1.D6
  N4: kEYPAD_MATRICIAL_1.arrow2, Part1.D5
  N5: kEYPAD_MATRICIAL_1.col3, Part1.D4
  N6: kEYPAD_MATRICIAL_1.arrow3, Part1.D3
  N7: kEYPAD_MATRICIAL_1.arrow4, Part1.D2
